// Logisim project Coa-Processor.circ as structural Verilog: 5 circuits, main circuit main
module main (
  input  [7:0] Pc_in
);

  wire Clock_out, Control_Unit_alu, Control_Unit_ir, Control_Unit_mem_read, Control_Unit_operand_fetch,
       Control_Unit_pc_enable, Control_Unit_r_w_prime, not_1_out, Reset;
  wire [3:0] IR_q, IR_q_2, IR_q_3, RAddress, RD, RS;
  wire [7:0] Accumulator, MAR_q, PC_pc_out, RA, Reg, Result;
  wire [15:0] RZ;
  wire [19:0] MBR_q, rom_1_data;

  Clock Clock (.out(Clock_out));
  LED led_1 (.in(Reset));
  Button button_1 (.out(Reset));
  control_unit Control_Unit (
    .Clock(Clock_out), .Reset(Reset), .PC_enable(Control_Unit_pc_enable), .Mem_read(Control_Unit_mem_read),
    .IR(Control_Unit_ir), .Operand_fetch(Control_Unit_operand_fetch), .ALU(Control_Unit_alu),
    .R_W_prime(Control_Unit_r_w_prime));
  not not_1 (not_1_out, Control_Unit_r_w_prime);
  Register u_RA (.D(Reg), .en(Control_Unit_operand_fetch), .Q(RA), .clk(Clock_out), .clr(Reset));
  pc PC (.PC_in(Pc_in), .PC_enable(Control_Unit_pc_enable), .Clock(Clock_out), .Reset(Reset), .PC_out(PC_pc_out));
  Register MAR (.D(PC_pc_out), .en(Control_Unit_pc_enable), .Q(MAR_q), .clk(Clock_out), .clr(Reset));
  ALU alu_1 (.A(RA), .B({IR_q_2, IR_q}), .S2_S1_S0(IR_q_3), .Y(RZ));
  ROM #(.dataWidth(20)) rom_1 (.addr(MAR_q), .data(rom_1_data));  // open: sel
  register register_1 (
    .D7D6___________D0(Result), .clk(Clock_out), .Accumulater(Accumulator), .R_W_prime(not_1_out),
    .S3S2S1S0(RAddress), .Output(Reg));
  Register #(.width(16)) u_RZ (.D(RZ), .en(Control_Unit_alu), .Q({Accumulator, Result}), .clk(Clock_out), .clr(Reset));
  Register #(.width(20)) MBR (.D(rom_1_data), .en(Control_Unit_mem_read), .Q(MBR_q), .clk(Clock_out), .clr(Reset));
  Register #(.width(20)) IR (
    .D(MBR_q), .en(Control_Unit_ir), .Q({IR_q_3, RD, RS, IR_q_2, IR_q}), .clk(Clock_out), .clr(Reset));
  Multiplexer #(.width(4), .enable("false")) multiplexer_1 (
    .in0(RS), .in1(RD), .out(RAddress), .sel(Control_Unit_r_w_prime));
  Hex_Digit_Display hex_digit_display_1 (.value(RA[7:4]));  // open: dp
  Hex_Digit_Display hex_digit_display_2 (.value(RA[3:0]));  // open: dp
  Hex_Digit_Display hex_digit_display_3 (.value(IR_q));  // open: dp
  Hex_Digit_Display hex_digit_display_4 (.value(IR_q_2));  // open: dp
  Hex_Digit_Display hex_digit_display_5 (.value(RZ[15:12]));  // open: dp
  Hex_Digit_Display hex_digit_display_6 (.value(RZ[11:8]));  // open: dp
  Hex_Digit_Display hex_digit_display_7 (.value(RZ[7:4]));  // open: dp
  Hex_Digit_Display hex_digit_display_8 (.value(RZ[3:0]));  // open: dp

  // Notes on the sheet:
  //   Code memory
  //   ALU
  //   Register bank
  //   contents of rom_1 (hex, n*v repeats v):
  //   1205 14506 27830 3ab02 4de01 5f001 61205 74503 87800 99a02 acd03 bf001 c2304
  //   Register Operand
  //   Immediate Operand
  //   Result
endmodule

module pc (
  input  [7:0] PC_in,
  input  PC_enable,
  input  Reset,
  input  Clock,
  output [7:0] PC_out
);

  wire [7:0] adder_1_out;

  Adder adder_1 (.a(PC_in), .b(PC_out), .out(adder_1_out));  // open: cin, cout
  Hex_Digit_Display hex_digit_display_1 (.value(PC_out[7:4]));  // open: dp
  Register register_1 (.D(adder_1_out), .en(PC_enable), .Q(PC_out), .clk(Clock), .clr(Reset));
  Hex_Digit_Display hex_digit_display_2 (.value(PC_out[3:0]));  // open: dp
endmodule

module control_unit (
  input  Clock,
  input  Reset,
  output PC_enable,
  output Mem_read,
  output IR,
  output Operand_fetch,
  output ALU,
  output R_W_prime
);

  wire [2:0] counter_1_q;

  Counter #(.width(3), .max('h7)) counter_1 (.Q(counter_1_q), .clk(Clock), .clr(Reset));  // open: load, D, count, carry
  Decoder #(.select(3), .enable("false")) decoder_1 (
    .out0(PC_enable), .out1(Mem_read), .out2(IR), .out3(Operand_fetch), .out4(ALU), .out5(R_W_prime),
    .sel(counter_1_q));  // open: out6, out7
endmodule

module ALU (
  input  [7:0] A,
  input  [7:0] B,
  input  [3:0] S2_S1_S0,
  output [15:0] Y
);

  wire adder_1_cout, adder_2_cout, subtractor_1_bout, subtractor_2_bout;
  wire [2:0] bit_extender_1_out, bit_extender_2_out, bit_extender_3_out, bit_extender_4_out;
  wire [3:0] bit_extender_16_out, bit_extender_16_out_2;
  wire [7:0] adder_1_out, adder_2_out, and_1_out, bit_extender_5_out, bit_extender_6_out, bit_extender_7_out,
       bit_extender_8_out, divider_1_out, divider_1_rem, multiplier_1_cout, multiplier_1_out, not_1_out,
       or_1_out, shifter_1_out, shifter_2_out, shifter_3_out, shifter_4_out, subtractor_1_out,
       subtractor_2_out;
  wire [15:0] bit_extender_9_out, bit_extender_10_out, bit_extender_11_out, bit_extender_12_out,
       bit_extender_13_out, bit_extender_14_out, bit_extender_15_out;

  Bit_Extender #(.out_width(3)) bit_extender_1 (.in(B), .out(bit_extender_1_out));
  Bit_Extender #(.out_width(3)) bit_extender_2 (.in(B), .out(bit_extender_2_out));
  Bit_Extender #(.out_width(3)) bit_extender_3 (.in(B), .out(bit_extender_3_out));
  Bit_Extender #(.out_width(3)) bit_extender_4 (.in(B), .out(bit_extender_4_out));
  Adder adder_1 (.a(A), .b(B), .out(adder_1_out), .cout(adder_1_cout));  // open: cin
  assign bit_extender_5_out = {{7{1'b0}}, adder_1_cout};  // Bit_Extender bit_extender_5
  Subtractor subtractor_1 (.a(A), .b(B), .out(subtractor_1_out), .bout(subtractor_1_bout));  // open: bin
  assign bit_extender_6_out = {{7{1'b0}}, subtractor_1_bout};  // Bit_Extender bit_extender_6
  Multiplier multiplier_1 (.a(A), .b(B), .out(multiplier_1_out), .cout(multiplier_1_cout));  // open: cin
  Divider divider_1 (.a(A), .b(B), .out(divider_1_out), .rem(divider_1_rem));  // open: upper
  Adder adder_2 (.a(A), .b(B), .out(adder_2_out), .cout(adder_2_cout));  // open: cin
  assign bit_extender_7_out = {{7{1'b0}}, adder_2_cout};  // Bit_Extender bit_extender_7
  Subtractor subtractor_2 (.a(A), .b(B), .out(subtractor_2_out), .bout(subtractor_2_bout));  // open: bin
  assign bit_extender_8_out = {{7{1'b0}}, subtractor_2_bout};  // Bit_Extender bit_extender_8
  assign and_1_out = A & B;  // AND_Gate and_1, 8 bits wide
  assign or_1_out = A | B;  // OR_Gate or_1, 8 bits wide
  assign not_1_out = ~A;  // NOT_Gate not_1, 8 bits wide
  Shifter #(.shift("lr")) shifter_1 (.in(A), .\dist (bit_extender_1_out), .out(shifter_1_out));
  Shifter shifter_2 (.in(A), .\dist (bit_extender_2_out), .out(shifter_2_out));
  Shifter #(.shift("rr")) shifter_3 (.in(A), .\dist (bit_extender_3_out), .out(shifter_3_out));
  Shifter #(.shift("rl")) shifter_4 (.in(A), .\dist (bit_extender_4_out), .out(shifter_4_out));
  assign bit_extender_9_out = {{8{1'b0}}, and_1_out};  // Bit_Extender bit_extender_9
  assign bit_extender_10_out = {{8{1'b0}}, or_1_out};  // Bit_Extender bit_extender_10
  assign bit_extender_11_out = {{8{1'b0}}, not_1_out};  // Bit_Extender bit_extender_11
  assign bit_extender_12_out = {{8{1'b0}}, shifter_1_out};  // Bit_Extender bit_extender_12
  assign bit_extender_13_out = {{8{1'b0}}, shifter_2_out};  // Bit_Extender bit_extender_13
  assign bit_extender_14_out = {{8{1'b0}}, shifter_3_out};  // Bit_Extender bit_extender_14
  assign bit_extender_15_out = {{8{1'b0}}, shifter_4_out};  // Bit_Extender bit_extender_15
  Multiplexer #(.select(4), .width(16), .enable("false")) multiplexer_1 (
    .in0({bit_extender_5_out, adder_1_out}), .in1({bit_extender_6_out, subtractor_1_out}),
    .in2({multiplier_1_cout, multiplier_1_out}), .in3({divider_1_rem, divider_1_out}),
    .in4({bit_extender_7_out, adder_2_out}), .in5({bit_extender_8_out, subtractor_2_out}),
    .in6(bit_extender_9_out), .in7(bit_extender_10_out), .in8(bit_extender_11_out),
    .in9(bit_extender_12_out), .in10(bit_extender_13_out), .in11(bit_extender_14_out),
    .in12(bit_extender_15_out), .out(Y), .sel(S2_S1_S0));  // open: in13, in14, in15
  Bit_Extender #(.in_width(16), .out_width(8)) bit_extender_16 (
    .in(Y), .out({bit_extender_16_out_2, bit_extender_16_out}));
  Hex_Digit_Display hex_digit_display_1 (.value(bit_extender_16_out_2));  // open: dp
  Hex_Digit_Display hex_digit_display_2 (.value(bit_extender_16_out));  // open: dp

  // Notes on the sheet:
  //   ALU and with 13 Operations
  //   Add-0
  //   Sub-01
  //   Mul-10
  //   Div-11
  //   Inc-100
  //   Dec-101
  //   Or-111
  //   Not-1000
  //   SHL-1010
  //   ROR-1011
  //   And-110
  //   SHR-1001
  //   ROL-1100
endmodule

// Reg-Bank
module register (
  input  [7:0] D7D6___________D0,
  input  clk,
  input  [7:0] Accumulater,
  input  R_W_prime,
  input  [3:0] S3S2S1S0,
  output [7:0] Output
);

  wire decoder_1_out0, decoder_1_out1, decoder_1_out2, decoder_1_out3, decoder_1_out4, decoder_1_out5,
       decoder_1_out6, decoder_1_out7, decoder_1_out8, decoder_1_out9, decoder_1_out10, decoder_1_out11,
       decoder_1_out12, decoder_1_out13, decoder_1_out14, decoder_1_out15, not_1_out;
  wire [7:0] register_1_q, register_2_q, register_3_q, register_4_q, register_5_q, register_6_q,
       register_7_q, register_8_q, register_9_q, register_10_q, register_11_q, register_12_q, register_13_q,
       register_14_q, register_15_q, register_16_q;

  not not_1 (not_1_out, R_W_prime);
  Register AC (.D(Accumulater), .en(not_1_out), .clk(clk));  // open: Q, clr
  Hex_Digit_Display hex_digit_display_1 (.value(D7D6___________D0[7:4]));  // open: dp
  Decoder #(.select(4), .disabled(0)) decoder_1 (
    .out0(decoder_1_out0), .out1(decoder_1_out1), .out2(decoder_1_out2), .out3(decoder_1_out3),
    .out4(decoder_1_out4), .out5(decoder_1_out5), .out6(decoder_1_out6), .out7(decoder_1_out7),
    .out8(decoder_1_out8), .out9(decoder_1_out9), .out10(decoder_1_out10), .out11(decoder_1_out11),
    .out12(decoder_1_out12), .out13(decoder_1_out13), .out14(decoder_1_out14), .out15(decoder_1_out15),
    .sel(S3S2S1S0), .en(not_1_out));
  Hex_Digit_Display hex_digit_display_2 (.value(D7D6___________D0[3:0]));  // open: dp
  Register register_1 (.D(D7D6___________D0), .en(decoder_1_out0), .Q(register_1_q), .clk(clk));  // open: clr
  Register register_2 (.D(D7D6___________D0), .en(decoder_1_out1), .Q(register_2_q), .clk(clk));  // open: clr
  Register register_3 (.D(D7D6___________D0), .en(decoder_1_out2), .Q(register_3_q), .clk(clk));  // open: clr
  Register register_4 (.D(D7D6___________D0), .en(decoder_1_out3), .Q(register_4_q), .clk(clk));  // open: clr
  Register register_5 (.D(D7D6___________D0), .en(decoder_1_out4), .Q(register_5_q), .clk(clk));  // open: clr
  Register register_6 (.D(D7D6___________D0), .en(decoder_1_out5), .Q(register_6_q), .clk(clk));  // open: clr
  Register register_7 (.D(D7D6___________D0), .en(decoder_1_out6), .Q(register_7_q), .clk(clk));  // open: clr
  Register register_8 (.D(D7D6___________D0), .en(decoder_1_out7), .Q(register_8_q), .clk(clk));  // open: clr
  Register register_9 (.D(D7D6___________D0), .en(decoder_1_out8), .Q(register_9_q), .clk(clk));  // open: clr
  Register register_10 (.D(D7D6___________D0), .en(decoder_1_out9), .Q(register_10_q), .clk(clk));  // open: clr
  Register register_11 (.D(D7D6___________D0), .en(decoder_1_out10), .Q(register_11_q), .clk(clk));  // open: clr
  Register register_12 (.D(D7D6___________D0), .en(decoder_1_out11), .Q(register_12_q), .clk(clk));  // open: clr
  Register register_13 (.D(D7D6___________D0), .en(decoder_1_out12), .Q(register_13_q), .clk(clk));  // open: clr
  Register register_14 (.D(D7D6___________D0), .en(decoder_1_out13), .Q(register_14_q), .clk(clk));  // open: clr
  Register register_15 (.D(D7D6___________D0), .en(decoder_1_out14), .Q(register_15_q), .clk(clk));  // open: clr
  Register register_16 (.D(D7D6___________D0), .en(decoder_1_out15), .Q(register_16_q), .clk(clk));  // open: clr
  Hex_Digit_Display hex_digit_display_3 (.value(Output[7:4]));  // open: dp
  Multiplexer #(.select(4), .width(8)) multiplexer_1 (
    .in0(register_1_q), .in1(register_2_q), .in2(register_3_q), .in3(register_4_q), .in4(register_5_q),
    .in5(register_6_q), .in6(register_7_q), .in7(register_8_q), .in8(register_9_q), .in9(register_10_q),
    .in10(register_11_q), .in11(register_12_q), .in12(register_13_q), .in13(register_14_q),
    .in14(register_15_q), .in15(register_16_q), .out(Output), .sel(S3S2S1S0), .en(R_W_prime));
  Hex_Digit_Display hex_digit_display_4 (.value(Output[3:0]));  // open: dp

  // Notes on the sheet:
  //   R0
  //   R1
  //   R2
  //   R3
  //   R4
  //   R5
  //   R6
  //   R7
  //   R8
  //   R9
  //   Ra
  //   Rb
  //   Rc
  //   Rd
  //   Re
  //   Rf
endmodule
